# Fritzing sketch LCD (saved by Fritzing 0.9.3b)
breadboards: 1

parts:
  Part5 = Arduino Uno (Rev3)
  LCM1602_IIC2 = LCM1602 IIC [part_number="LCM1602 IIC" chip_label="LCM1602 IIC" package="DIP (Dual Inline) [THT]"]
  U4 = LCD-16X2 [package=lcd-16x2_nosilk]

nets:
  N1: Part5.A4/SDA, LCM1602_IIC2.SDA
  N2: Part5.A5/SCL, LCM1602_IIC2.SCL
  5V: Part5.5V, LCM1602_IIC2.VCC
  GND: Part5.GND, LCM1602_IIC2.GND
  VSS: LCM1602_IIC2.VSS, U4.VSS
  VDD: LCM1602_IIC2.VDD, U4.VDD
  N3: LCM1602_IIC2.V0, U4.VO
  N4: LCM1602_IIC2.RS, U4.RS
  N5: LCM1602_IIC2.RW, U4.R_W
  N6: LCM1602_IIC2.E, U4.E
  N7: LCM1602_IIC2.D0, U4.DB0
  N8: LCM1602_IIC2.D1, U4.DB1
  N9: LCM1602_IIC2.D2, U4.DB2
  N10: LCM1602_IIC2.D3, U4.DB3
  N11: LCM1602_IIC2.D4, U4.DB4
  N12: LCM1602_IIC2.D5, U4.DB5
  N13: LCM1602_IIC2.D6, U4.DB6
  N14: LCM1602_IIC2.D7, U4.DB7
  N15: LCM1602_IIC2.A, U4.A
  N16: LCM1602_IIC2.K, U4.K

custom parts:
  LCM1602 IIC: I2C-Module to use a 1602 or 2004 LCD on with the wire.h libory Serial LCD Modul
