# Fritzing sketch buzzer (saved by Fritzing 0.9.3b)
breadboards: 1

parts:
  Part1 = Arduino Uno (Rev3)
  Part2 = KY-012 Active Buzzer Module [package="Breakout board"]

nets:
  N1: Part1.A5/SCL, Part2.S
  N2: Part1.GND, Part2.-

custom parts:
  KY-012 Active Buzzer Module: Active Piezoelectric Buzzer Module Keyes KY-012, it produces single-tone sound when signal is high.
